// Logisim project Tema esame 20-09-2023  - Esercizio 2.circ as structural Verilog: 3 circuits, main circuit main
module main (
  input  Input,
  output out_2
);

  wire clock_1_out, d_ff_1_q, d_ff_2_q, nextstate_1_nxt0, nextstate_1_nxt1;

  Clock clock_1 (.out(clock_1_out));
  D_Flip_Flop d_ff_1 (.clk(clock_1_out), .D(nextstate_1_nxt0), .Q(d_ff_1_q));  // open: Qn, preset, en, reset
  D_Flip_Flop d_ff_2 (.clk(clock_1_out), .D(nextstate_1_nxt1), .Q(d_ff_2_q));  // open: Qn, preset, en, reset
  Output output_1 (.S0(d_ff_1_q), .S1(d_ff_2_q), .Output(out_2));
  NextState nextstate_1 (.S0(d_ff_1_q), .S1(d_ff_2_q), .Input(Input), .NXT0(nextstate_1_nxt0), .NXT1(nextstate_1_nxt1));
endmodule

module Output (
  input  S0,
  input  S1,
  output Output
);


  assign Output = S0;
  // also tied to GND on the sheet: S1
endmodule

module NextState (
  input  S0,
  input  S1,
  input  Input,
  output NXT0,
  output NXT1
);

  wire and_1_out, and_2_out, and_3_out, and_4_out;

  and and_1 (and_1_out, S0, Input);
  and and_2 (and_2_out, S1, Input);
  and and_3 (and_3_out, ~S0, ~S1, Input);  // AND_Gate
  and and_4 (and_4_out, S0, ~Input);  // AND_Gate
  or or_1 (NXT0, and_1_out, and_2_out);
  or or_2 (NXT1, and_3_out, and_4_out);
endmodule
